# Fritzing sketch layout (saved by Fritzing 0.6.3b)
breadboards: 2
perfboards: 1

parts:
  S1 = Pushbutton [package="[THT]"]
  S2 = Pushbutton [package="[THT]"]
  S3 = Pushbutton [package="[THT]"]
  S4 = Pushbutton [package="[THT]"]
  LCD1 = LCD screen
  R1 = Resistor [tolerance=±5% resistance=10k package=THT]
  R2 = Resistor [tolerance=±5% resistance=10k package=THT]
  R3 = Resistor [tolerance=±5% resistance=10k package=THT]
  R4 = Resistor [tolerance=±5% resistance=10k package=THT]
  Y1 = Resonator [frequency="16 Mhz" package=THT]
  R5 = Trimmer Potentiometer [maximum_resistance=10kΩ package=THT]
  LCD2 = LCD screen  # not connected
  S5 = Pushbutton [package="[THT]"]
  S6 = Pushbutton [package="[THT]"]
  S7 = Pushbutton [package="[THT]"]
  S8 = Pushbutton [package="[THT]"]
  IC2 = IC, DIP package, 40 pins [chip_label=IC spacing=300mil]  # not connected
  R7 = Resistor [tolerance=±5% resistance=10k package=THT]  # not connected
  R8 = Resistor [tolerance=±5% resistance=10k package=THT]  # not connected
  R9 = Resistor [tolerance=±5% resistance=10k package=THT]  # not connected
  R10 = Resistor [tolerance=±5% resistance=10k package=THT]  # not connected
  R11 = Trimmer Potentiometer [maximum_resistance=10kΩ package=THT]  # not connected
  J1 = female pin header, 2 pins [form="♀ (female)"]  # not connected
  S9 = Toggle Switch [package=THT]
  S12 = Pushbutton [package="[THT]"]
  R13 = Resistor [tolerance=±5% resistance=10k package=THT]
  R12 = Resistor [tolerance=±5% resistance=10k package=THT]
  S13 = Pushbutton [package="[THT]"]
  S11 = Pushbutton [package="[THT]"]
  R14 = Resistor [tolerance=±5% resistance=10k package=THT]
  R16 = Trimmer Potentiometer [maximum_resistance=10kΩ package=THT]
  LCD3 = LCD screen
  S10 = Pushbutton [package="[THT]"]
  S14 = Toggle Switch [package=THT]
  R15 = Resistor [tolerance=±5% resistance=10k package=THT]
  Arduino1 = Arduino
  IC1 = IC, DIP package, 28 pins [chip_label=IC spacing=300mil]

nets:
  N1: S1.Pin_1, S1.Pin_2, R1.Pin_1
  N2: S1.Pin_3, S1.Pin_4, S2.Pin_3, S2.Pin_4, S3.Pin_3, S3.Pin_4, S4.Pin_3, S4.Pin_4, Y1.GND, IC1.pin8
  N3: S2.Pin_1, S2.Pin_2, R2.Pin_1
  N4: S3.Pin_1, S3.Pin_2, R3.Pin_1
  N5: S4.Pin_1, S4.Pin_2, R4.Pin_1
  N6: LCD1.VSS, LCD1.R/W, LCD1.LED-, R5.leg2
  N7: LCD1.VDD, R5.leg1
  N8: LCD1.V0, R5.wiper
  N9: LCD1.LED+, S9.L2
  N10: R1.Pin_0, R2.Pin_0, R3.Pin_0, R4.Pin_0, S9.COM, IC1.pin7
  N11: Y1.0, IC1.pin9
  N12: Y1.pin_1, IC1.pin10
  N13: S5.Pin_1, S5.Pin_2
  N14: S5.Pin_3, S5.Pin_4
  N15: S6.Pin_1, S6.Pin_2
  N16: S6.Pin_3, S6.Pin_4
  N17: S7.Pin_1, S7.Pin_2
  N18: S7.Pin_3, S7.Pin_4
  N19: S8.Pin_1, S8.Pin_2
  N20: S8.Pin_3, S8.Pin_4
  N21: S12.Pin_1, S12.Pin_2, R14.Pin_1, Arduino1.D12
  N22: S12.Pin_3, S12.Pin_4, S13.Pin_3, S13.Pin_4, S11.Pin_3, S11.Pin_4
  N23: R13.Pin_0, R12.Pin_0, R14.Pin_0, S14.COM, R15.Pin_0
  N24: R13.Pin_1, S11.Pin_1, S11.Pin_2, Arduino1.D11
  N25: R12.Pin_1, S10.Pin_1, S10.Pin_2, Arduino1.D10
  N26: S13.Pin_1, S13.Pin_2, R15.Pin_1, Arduino1.D13
  N27: R16.leg1, LCD3.VDD
  N28: R16.wiper, LCD3.V0
  N29: R16.leg2, LCD3.VSS, LCD3.R/W, LCD3.LED-
  N30: LCD3.RS, Arduino1.A0
  N31: LCD3.E, Arduino1.A1
  N32: LCD3.DB4, Arduino1.A2
  N33: LCD3.DB5, Arduino1.A3
  N34: LCD3.DB6, Arduino1.A4
  N35: LCD3.DB7, Arduino1.A5
  N36: LCD3.LED+, S14.L2
  N37: S10.Pin_3, S10.Pin_4
