# Fritzing sketch placa_topos (saved by Fritzing 0.6.5b)
perfboards: 1

parts:
  LCD2 = LCD screen
  S1 = Pushbutton [package="[THT]"]
  S3 = Pushbutton [package="[THT]"]
  R1 = Resistor [tolerance=±5% resistance=10k package=THT]
  R2 = Resistor [tolerance=±5% resistance=10k package=THT]
  R3 = Resistor [tolerance=±5% resistance=10k package=THT]
  R4 = Resistor [tolerance=±5% resistance=10k package=THT]
  R11 = Trimmer Potentiometer [maximum_resistance=10kΩ package=THT]
  S4 = Pushbutton [package="[THT]"]
  S10 = Toggle Switch [package=THT]
  J1 = female pin header, 4 pins [form="♀ (female)"]
  S2 = Pushbutton [package="[THT]"]
  IC2 = IC, DIP package, 28 pins [chip_label=IC spacing=300mil]

nets:
  N1: LCD2.VSS, LCD2.LED-, R1.Pin_1, R2.Pin_1, R3.Pin_1, R4.Pin_1, R11.leg2, S10.L2
  N2: LCD2.VDD, LCD2.LED+, S1.Pin_3, S1.Pin_4, S3.Pin_3, S3.Pin_4, R11.leg1, S4.Pin_3, S4.Pin_4, S10.COM, J1.pin1, S2.Pin_1, S2.Pin_2, IC2.pin7
  N3: LCD2.V0, R11.wiper
  N4: LCD2.RS, IC2.pin24
  N5: LCD2.E, IC2.pin19
  N6: LCD2.DB4, IC2.pin18
  N7: LCD2.DB5, IC2.pin17
  N8: LCD2.DB6, IC2.pin16
  N9: LCD2.DB7, IC2.pin15
  N10: S1.Pin_1, S1.Pin_2, R1.Pin_0, IC2.pin25
  N11: S3.Pin_1, S3.Pin_2, R3.Pin_0, IC2.pin27
  N12: R2.Pin_0, S2.Pin_3, S2.Pin_4, IC2.pin26
  N13: R4.Pin_0, S4.Pin_1, S4.Pin_2, IC2.pin28
